# Fritzing sketch SEMAFORO_PRACTICA_1 (saved by Fritzing 0.9.3b)
breadboards: 1

parts:
  LED1 = LED - 5mm [color="Red (633nm)" package="5 mm [THT]"]
  LED2 = LED - 5mm [color="Yellow (595nm)" package="5 mm [THT]"]
  LED3 = LED - 5mm [color="Green (570nm)" package="5 mm [THT]"]
  LED4 = LED - 5mm [color="Red (633nm)" package="5 mm [THT]"]
  LED5 = LED - 5mm [color="Green (570nm)" package="5 mm [THT]"]
  S1 = Pushbutton [package=THT]
  R1 = Resistor [tolerance=±5% resistance=2.2k package=THT]
  R2 = Resistor [tolerance=±5% resistance=2.2k package=THT]
  R3 = Resistor [tolerance=±5% resistance=2.2k package=THT]
  R4 = Resistor [tolerance=±5% resistance=2.2k package=THT]
  R5 = Resistor [tolerance=±5% resistance=2.2k package=THT]
  Componente1 = Arduino Uno (Rev3) - ICSP
  R6 = Resistor [tolerance=±5% resistance=2.2k package=THT]

nets:
  N1: LED1.cathode, LED2.cathode, LED3.cathode, LED4.cathode, LED5.cathode, S1.leg1, Componente1.GND
  N2: LED1.anode, R5.Pin_0, Componente1.D13/SCK
  N3: LED2.anode, R2.Pin_0, Componente1.D12/MISO
  N4: LED3.anode, R1.Pin_0, Componente1.D11_PWM/MOSI
  N5: LED4.anode, R4.Pin_0, Componente1.D9_PWM
  N6: LED5.anode, R3.Pin_0, Componente1.D10_PWM/SS
  N7: S1.leg0, Componente1.D2, R6.Pin_0
  N8: R1.Pin_1, R2.Pin_1, R3.Pin_1, R4.Pin_1, R5.Pin_1, Componente1.5V, R6.Pin_1

// code stored in the sketch: SEMAFORO.ino
int sensorPin = A0;
int boton =2;
int sensorValue; 
int rapidez;
void setup() {
  // put your setup code here, to run once:
  pinMode(boton,INPUT);
  pinMode(9,OUTPUT);// ROJO PEATON
  pinMode(10,OUTPUT);// VERDE PEATON
  pinMode(11,OUTPUT);// VERDE CARRO
  pinMode(12,OUTPUT);// AMARILLO CARRO
  pinMode(13,OUTPUT);// ROJO CARRO
  //delay(rapidez);

}

void loop() {
  sensorValue = analogRead(sensorPin);
  rapidez = map(sensorValue, 0,70,0,500);
  // put your main code here, to run repeatedly:
digitalWrite(11, HIGH); // VERDE CARRO ENCENDIDO
digitalWrite(9, HIGH); // ROJO PEATON ENCENDIDO

if(digitalRead(boton)==LOW){
digitalWrite(11,LOW);// VERDE CARRO APAGADO
digitalWrite(12,HIGH);// AMARILLO CARRO ENCENDIDO
delay(2500);
digitalWrite(12,LOW);// AMARILLO CARRO APAGADO
digitalWrite(13,HIGH);// ROJO CARRO ENCENDIDO
digitalWrite(9,LOW);// ROJO PEATON APAGADO
digitalWrite(10,HIGH);// VERDE PEATON ENCENDIDO
delay(8000);
//delay(rapidez);
digitalWrite(10,LOW);// VERDE PEATON APAGADO
digitalWrite(13,LOW);// ROJO CARRO APAGADO

}
}
